// Logisim project Counter同步复位.circ as structural Verilog: 1 circuit, main circuit main
module main (
  input  reset,
  input  WE,
  output [1:0] count
);

  wire and_1_out, clock_1_out, not_1_out;

  not not_1 (not_1_out, reset);
  Clock clock_1 (.out(clock_1_out));
  and and_1 (and_1_out, WE, not_1_out);
  Counter #(.width(2), .max('h3)) counter_1 (
    .load(reset), .D(2'b00), .count(and_1_out), .Q(count), .clk(clock_1_out));  // open: carry, clr
endmodule
