// Logisim project Register初值.circ as structural Verilog: 1 circuit, main circuit main
module main (
  input  [2:0] in_1,
  output [2:0] out_2
);

  wire clock_1_out;
  wire [2:0] register_1_q, xor_1_out;

  assign xor_1_out = in_1 ^ 3'b111;  // XOR_Gate xor_1, 3 bits wide
  Clock clock_1 (.out(clock_1_out));
  Register #(.width(3)) register_1 (.D(xor_1_out), .Q(register_1_q), .clk(clock_1_out));  // open: en, clr
  assign out_2 = register_1_q ^ 3'b111;  // XOR_Gate xor_2, 3 bits wide
endmodule
