// Logisim project Register同步复位.circ as structural Verilog: 1 circuit, main circuit main
module main (
  input  reset,
  input  [7:0] \input ,
  input  WE,
  input  clk,
  output [7:0] out
);

  wire or_1_out;
  wire [7:0] multiplexer_1_out;

  Multiplexer #(.width(8), .enable("false")) multiplexer_1 (
    .in0(\input ), .in1({8{1'b0}}), .out(multiplexer_1_out), .sel(reset));
  or or_1 (or_1_out, WE, reset);
  Register register_1 (.D(multiplexer_1_out), .en(or_1_out), .Q(out), .clk(clk));  // open: clr

  // Other names for the same wires on the sheet: output[7:0] = out; write_enable = WE
endmodule
