// Logisim project 三态线或.circ as structural Verilog: 1 circuit, main circuit main
module main (
  input  in_1,
  input  in_2,
  input  in_3,
  output out_4
);

  wire buffer_1_out;

  buf buffer_1 (buffer_1_out, in_1);
  buf buffer_2 (buffer_1_out, in_2);
  buf buffer_3 (buffer_1_out, in_3);
  Pull_Resistor pull_resistor_1 (.node(buffer_1_out));
  assign out_4 = buffer_1_out ? 1'b1 : 1'bz;  // Controlled_Buffer controlled_buffer_1

  // Notes on the sheet:
  //   真值表：A B = 00 → Y=0；01 → Y=1；10 → Y=1；11 → Y=1。
  //   实验：删除第二路或第三路的下拉，把 A、B 都设成 0，该路输出会浮空；普通 OR 仍为 0。
  //   所有并线的驱动器只输出 1 或 Z，因此没有“一个输出 0、另一个输出 1”的冲突。
  //   这里只演示组合逻辑，不需要时钟。下拉是默认电平，并非用来延迟信号。
  //   buffer_1 drives only 1 and floats otherwise
  //   buffer_2 drives only 1 and floats otherwise
  //   buffer_3 drives only 1 and floats otherwise
  //   下面的三角形有使能端；上面的普通 Buffer 没有使能端，但修改了输出方式。
endmodule
